// Logisim project alu.circ as structural Verilog: 1 circuit, main circuit alu
module alu (
  input  [31:0] A,
  input  [31:0] B,
  input  [3:0] ALUSel,
  input  [30:0] in_4,
  output [31:0] Result
);

  wire [0:0] slt;
  wire [31:0] add, and1, divu, mul, mulh, mulhu, or1, remu, sll1, sra1, srl1, sub, vaddh, xor1;

  Adder #(.width(32)) adder_1 (.a(A), .b(B), .out(add));  // open: cin, cout
  Subtractor #(.width(32)) subtractor_1 (.a(A), .b(B), .out(sub));  // open: bin, bout
  Multiplier #(.width(32)) multiplier_1 (.a(A), .b(B), .out(mul), .cout(mulh));  // open: cin
  Divider #(.width(32)) divider_1 (.a(A), .b(B), .out(divu), .rem(remu));  // open: upper
  assign xor1 = A ^ B;  // XOR_Gate xor_1, 32 bits wide
  assign or1 = A | B;  // OR_Gate or_1, 32 bits wide
  assign and1 = A & B;  // AND_Gate and_1, 32 bits wide
  Shifter #(.width(32)) shifter_1 (.in(A), .\dist (B[4:0]), .out(sll1));
  Shifter #(.width(32), .shift("ar")) shifter_2 (.in(A), .\dist (B[4:0]), .out(sra1));
  Shifter #(.width(32), .shift("lr")) shifter_3 (.in(A), .\dist (B[4:0]), .out(srl1));
  Comparator #(.width(32)) comparator_1 (.a(A), .b(B), .lt(slt[0]));  // open: gt, eq
  Multiplier #(.width(32)) multiplier_2 (.a(A), .b(B), .cout(mulhu));  // open: out, cin
  Adder #(.width(16)) adder_2 (.a(A[15:0]), .b(B[15:0]), .out(vaddh[15:0]));  // open: cin, cout
  Adder #(.width(16)) adder_3 (.a(A[31:16]), .b(B[31:16]), .out(vaddh[31:16]));  // open: cin, cout
  Multiplexer #(.select(4), .width(32), .enable("false")) multiplexer_1 (
    .in0(add), .in1(and1), .in2(or1), .in3(xor1), .in4(srl1), .in5(sra1), .in6(sll1), .in7({in_4, slt[0]}),
    .in8(divu), .in9(remu), .in10(mul), .in11(mulhu), .in12(sub), .in13(B), .in14(mulh), .in15(vaddh),
    .out(Result), .sel(ALUSel));

  // Other names for the same wires on the sheet: bsel[31:0] = B; slt[31:1] = in_4

  // Notes on the sheet:
  //   INPUTS to your circuit
  //   DON'T CHANGE THE LOCATIONS OF THE INPUTS AND OUTPUTS!
  //   OUTPUT from your circuit
endmodule
