// Logisim project cpu.circ as structural Verilog: 12 circuits, main circuit main
module main (
  input  [31:0] INSTRUCTION,
  input  CLOCK,
  output [31:0] FETCH_ADDRESS,
  output [31:0] ra,
  output [31:0] sp,
  output [31:0] t0,
  output [31:0] t1,
  output [31:0] t2,
  output [31:0] s0,
  output [31:0] s1,
  output [31:0] a0,
  output [31:0] out_12,
  output [1:0] out_13,
  output [3:0] out_14,
  output [4:0] rd,
  output [6:0] out_16,
  output [2:0] funct3,
  output [4:0] rs1,
  output [4:0] rs2,
  output [6:0] funct7
);

  wire and_1_out, ASel, BrEq, BrLt, BrUn, BSel, comparator_1_eq, comparator_2_eq, comparator_3_eq,
       comparator_4_eq, comparator_5_eq, MemRW, or_1_out, PCSel, RWEn;
  wire [2:0] ImmSel;
  wire [4:0] multiplexer_3_out;
  wire [31:0] adder_2_out, DMEM_read_data, immediate, multiplexer_1_out, multiplexer_2_out,
       multiplexer_4_out, multiplexer_5_out, multiplexer_6_out, multiplexer_7_out, PC, PCPLUS4,
       RegFile_read_data_1, RegWB, WriteData;

  Adder #(.width(32)) adder_1 (.a(FETCH_ADDRESS), .b(32'h4), .out(PCPLUS4));  // open: cin, cout
  Multiplexer #(.width(32), .enable("false")) multiplexer_1 (
    .in0(PCPLUS4), .in1(out_12), .out(multiplexer_1_out), .sel(PCSel));
  Multiplexer #(.width(32), .enable("false")) multiplexer_2 (
    .in0(INSTRUCTION), .in1(32'h13), .out(multiplexer_2_out), .sel(or_1_out));
  Comparator #(.width(7)) comparator_1 (.a(7'b1100111), .b(out_16), .eq(comparator_1_eq));  // open: gt, lt
  Comparator #(.width(7)) comparator_2 (.a(out_16), .b(7'b1101111), .eq(comparator_2_eq));  // open: gt, lt
  Register #(.width(32)) u_PC (.D(multiplexer_1_out), .en(1'b1), .Q(FETCH_ADDRESS), .clk(CLOCK));  // open: clr
  Register #(.width(32)) register_1 (
    .D(multiplexer_2_out), .en(1'b1), .Q({funct7, rs2, rs1, funct3, rd, out_16}), .clk(CLOCK));  // open: clr
  Comparator #(.width(7)) comparator_3 (.a(7'b1100011), .b(out_16), .eq(comparator_3_eq));  // open: gt, lt
  Control control_1 (
    .BrEq(BrEq), .BrLt(BrLt), .in_1({funct7, rs2, rs1, funct3, rd, out_16}), .ImmSel(ImmSel),
    .ALUSel(out_14), .WBSel(out_13), .PCSel(PCSel), .RWEn(RWEn), .ASel(ASel), .BSel(BSel), .MemRW(MemRW),
    .BrUn(BrUn));  // open: out_13
  or or_1 (or_1_out, comparator_1_eq, and_1_out, comparator_2_eq);
  Comparator #(.width(7)) comparator_4 (.a(out_16), .b(7'b0100011), .eq(comparator_4_eq));  // open: gt, lt
  and and_1 (and_1_out, comparator_3_eq, PCSel);
  Register #(.width(32)) register_2 (.D(FETCH_ADDRESS), .en(1'b1), .Q(PC), .clk(CLOCK));  // open: clr
  Multiplexer #(.width(5), .enable("false")) multiplexer_3 (
    .in0(rd), .in1(rs2), .out(multiplexer_3_out), .sel(comparator_4_eq));
  // Probe on RegWB
  ImmediateGen immediategen_1 (.Instruction({funct7, rs2, rs1, funct3, rd, out_16}), .out_2(immediate));
  regfile_main RegFile (
    .rs2(rs2), .rd(multiplexer_3_out), .Read_Data_1(RegFile_read_data_1), .Read_Data_2(WriteData), .ra(ra),
    .sp(sp), .t0(t0), .t1(t1), .t2(t2), .s0(s0), .s1(s1), .a0(a0), .rs1(rs1), .Write_Data(RegWB),
    .RegWEn(RWEn), .clk(CLOCK));
  // Probe on RegFile_read_data_1
  // Probe on WriteData
  Register #(.width(32)) register_3 (.D(immediate), .en(1'b1), .clk(CLOCK));  // open: Q, clr
  BranchComp branchcomp_1 (.rs1(RegFile_read_data_1), .rs2(WriteData), .EQ(BrEq), .LT(BrLt), .BrUn(BrUn));  // open: GT
  Multiplexer #(.width(32), .enable("false")) multiplexer_4 (
    .in0(PC), .in1(RegFile_read_data_1), .out(multiplexer_4_out), .sel(ASel));
  Multiplexer #(.width(32), .enable("false")) multiplexer_5 (
    .in0(WriteData), .in1(immediate), .out(multiplexer_5_out), .sel(BSel));
  Multiplexer #(.width(32), .enable("false")) multiplexer_6 (
    .in0(multiplexer_4_out), .in1(multiplexer_5_out), .out(multiplexer_6_out), .sel(comparator_5_eq));
  Multiplexer #(.width(32), .enable("false")) multiplexer_7 (
    .in0(multiplexer_5_out), .in1(32'hc), .out(multiplexer_7_out), .sel(comparator_5_eq));
  Comparator #(.width(5)) comparator_5 (.a(out_16[6:2]), .b(5'b01101), .eq(comparator_5_eq));  // open: gt, lt
  alu Arithmetic_Logic_Unit (
    .A(multiplexer_6_out), .B(multiplexer_7_out), .ALUSel(out_14), .in_4({31{1'b0}}), .Result(out_12));
  Adder #(.width(32)) adder_2 (.a(PC), .b(32'h4), .out(adder_2_out));  // open: cin, cout
  mem_main DMEM (.Address(WriteData), .Write_Data(out_12), .Write_En(MemRW), .Read_Data(DMEM_read_data), .clk(CLOCK));
  Multiplexer #(.select(2), .width(32), .enable("false")) multiplexer_8 (
    .in0(adder_2_out), .in1(out_12), .in2(DMEM_read_data), .out(RegWB), .sel(out_13));  // open: in3

  // Other names for the same wires on the sheet: opcode[6:0] = out_16; Opcode26[4:0] = out_16[6:2];
  //   ALUEX[31:0] = out_12; ALUSel[3:0] = out_14; clk = CLOCK; PROGRAM_COUNTER[31:0] = FETCH_ADDRESS;
  //   WBSel[1:0] = out_13

  // Notes on the sheet:
  //   Technically this is IMEM (IF)
  //   Output
  //   Inputs/Outputs from run.circ. DO NOT MOVE THESE.
  //   Inputs
  //   if instruction is a jump then don't write to pc. If instruction is a branch then don't write if the branch is true. In both cases, send a nop into the instruction. (use a mux with nop and instruction)
  //   Inputs/Outputs from run.circ. DO NOT MOVE THESE.
endmodule

module Control (
  input  [31:0] in_1,
  input  BrEq,
  input  BrLt,
  output [3:0] ALUSel,
  output PCSel,
  output RWEn,
  output ASel,
  output [2:0] ImmSel,
  output BSel,
  output MemRW,
  output BrUn,
  output [1:0] WBSel,
  output [1:0] out_13
);

  wire and_1_out, and_3_out, and_4_out, and_6_out, branch, comparator_1_eq, comparator_2_eq, comparator_3_eq,
       comparator_3_lt, comparator_4_eq, comparator_5_eq, comparator_6_eq, comparator_7_eq, comparator_8_eq,
       comparator_9_eq, comparator_10_eq, comparator_11_eq, comparator_12_eq, comparator_13_eq,
       comparator_14_eq, comparator_15_eq, comparator_16_eq, comparator_18_eq, comparator_19_eq,
       comparator_20_eq, comparator_21_eq, comparator_22_eq, comparator_23_eq, comparator_24_eq,
       comparator_25_eq, comparator_26_eq, comparator_27_eq, comparator_28_eq, comparator_29_eq,
       comparator_30_eq, not_1_out, or_1_out, or_2_out;
  wire [1:0] adder_1_out, alu1, bit_extender_1_out, bit_extender_2_out, bit_extender_4_out,
       bit_extender_5_out, bit_extender_6_out, mem2, multiplier_1_out, or_5_out, or_7_out, subtractor_1_out;

  not not_1 (not_1_out, BrEq);
  and and_1 (and_1_out, BrEq, comparator_3_eq);
  Comparator #(.width(7)) comparator_1 (.a(7'b0110011), .b(in_1[6:0]), .eq(comparator_1_eq));  // open: gt, lt
  Comparator #(.width(3)) comparator_2 (.a(in_1[14:12]), .b(3'b001), .eq(comparator_2_eq));  // open: gt, lt
  Comparator #(.width(3)) comparator_3 (
    .a(in_1[14:12]), .b(3'b000), .eq(comparator_3_eq), .lt(comparator_3_lt));  // open: gt
  Comparator #(.width(3)) comparator_4 (.a(in_1[14:12]), .b(3'b100), .eq(comparator_4_eq));  // open: gt, lt
  Comparator #(.width(3)) comparator_5 (.a(in_1[14:12]), .b(3'b110), .eq(comparator_5_eq));  // open: gt, lt
  Comparator #(.width(7)) comparator_6 (.a(7'b0010011), .b(in_1[6:0]), .eq(comparator_6_eq));  // open: gt, lt
  and and_2 (branch, not_1_out, comparator_2_eq);
  and and_3 (and_3_out, BrLt, comparator_5_eq);
  and and_4 (and_4_out, BrLt, comparator_4_eq);
  Comparator #(.width(7)) comparator_7 (.a(7'b1100011), .b(in_1[6:0]), .eq(comparator_7_eq));  // open: gt, lt
  Comparator #(.width(7)) comparator_8 (.a(7'b1100111), .b(in_1[6:0]), .eq(comparator_8_eq));  // open: gt, lt
  Comparator #(.width(7)) comparator_9 (.a(7'b1101111), .b(in_1[6:0]), .eq(comparator_9_eq));  // open: gt, lt
  Comparator #(.width(7)) comparator_10 (.a(in_1[6:0]), .b(7'b0100011), .eq(comparator_10_eq));  // open: gt, lt
  Comparator #(.width(7)) comparator_11 (.a(in_1[6:0]), .b(7'b1100011), .eq(comparator_11_eq));  // open: gt, lt
  Comparator #(.width(7)) comparator_12 (.a(7'b0000011), .b(in_1[6:0]), .eq(comparator_12_eq));  // open: gt, lt
  Comparator #(.width(7)) comparator_13 (.a(7'b0010011), .b(in_1[6:0]), .eq(comparator_13_eq));  // open: gt, lt
  Comparator #(.width(7)) comparator_14 (.a(7'b1100111), .b(in_1[6:0]), .eq(comparator_14_eq));  // open: gt, lt
  Comparator #(.width(7)) comparator_15 (.a(7'b0110111), .b(in_1[6:0]), .eq(comparator_15_eq));  // open: gt, lt
  Comparator #(.width(7)) comparator_16 (.a(7'b1101111), .b(in_1[6:0]), .eq(comparator_16_eq));  // open: gt, lt
  Comparator #(.width(7)) comparator_17 (.a(in_1[6:0]), .b(7'b0100011), .eq(MemRW));  // open: gt, lt
  Comparator #(.width(7)) comparator_18 (.a(in_1[6:0]), .b(7'b1100011), .eq(comparator_18_eq));  // open: gt, lt
  Comparator #(.width(3)) comparator_19 (.a(in_1[14:12]), .b(3'b110), .eq(comparator_19_eq));  // open: gt, lt
  Comparator #(.width(7)) comparator_20 (.a(7'b1100111), .b(in_1[6:0]), .eq(comparator_20_eq));  // open: gt, lt
  Comparator #(.width(7)) comparator_21 (.a(7'b1101111), .b(in_1[6:0]), .eq(comparator_21_eq));  // open: gt, lt
  or or_1 (or_1_out, comparator_10_eq, comparator_11_eq);
  Comparator #(.width(7)) comparator_22 (.a(in_1[6:0]), .b(7'b1100111), .eq(comparator_22_eq));  // open: gt, lt
  Comparator #(.width(7)) comparator_23 (.a(7'b0100011), .b(in_1[6:0]), .eq(comparator_23_eq));  // open: gt, lt
  and and_5 (BrUn, comparator_18_eq, comparator_19_eq);
  assign bit_extender_1_out = {{1{1'b0}}, comparator_20_eq};  // Bit_Extender bit_extender_1
  assign bit_extender_2_out = {{1{1'b0}}, comparator_21_eq};  // Bit_Extender bit_extender_2
  Comparator #(.width(7)) comparator_24 (.a(7'b0010011), .b(in_1[6:0]), .eq(comparator_24_eq));  // open: gt, lt
  Comparator #(.width(7)) comparator_25 (.a(7'b0110011), .b(in_1[6:0]), .eq(comparator_25_eq));  // open: gt, lt
  Comparator #(.width(7)) comparator_26 (.a(7'b0110111), .b(in_1[6:0]), .eq(comparator_26_eq));  // open: gt, lt
  or or_2 (or_2_out, branch, and_4_out, and_3_out, and_1_out);
  Comparator #(.width(7)) comparator_27 (.a(in_1[6:0]), .b(7'b1100011), .eq(comparator_27_eq));  // open: gt, lt
  not not_2 (RWEn, or_1_out);
  Comparator #(.width(7)) comparator_28 (.a(7'b0000011), .b(in_1[6:0]), .eq(comparator_28_eq));  // open: gt, lt
  Comparator #(.width(7)) comparator_29 (.a(7'b0000011), .b(in_1[6:0]), .eq(comparator_29_eq));  // open: gt, lt
  and and_6 (and_6_out, branch, comparator_7_eq);
  or or_3 (ASel, comparator_22_eq, comparator_23_eq, comparator_1_eq, comparator_6_eq, comparator_28_eq);
  or or_4 (BSel, comparator_14_eq, comparator_12_eq, comparator_13_eq, comparator_15_eq, comparator_16_eq, comparator_30_eq);
  assign or_5_out = bit_extender_1_out | bit_extender_2_out;  // OR_Gate or_5, 2 bits wide
  assign alu1 = {{1{1'b0}}, branch};  // Bit_Extender bit_extender_3
  assign bit_extender_4_out = {{1{1'b0}}, comparator_24_eq};  // Bit_Extender bit_extender_4
  assign bit_extender_5_out = {{1{1'b0}}, comparator_25_eq};  // Bit_Extender bit_extender_5
  assign bit_extender_6_out = {{1{1'b0}}, comparator_26_eq};  // Bit_Extender bit_extender_6
  assign mem2 = {{1{1'b0}}, comparator_29_eq};  // Bit_Extender bit_extender_7
  and and_7 (branch, or_2_out, comparator_27_eq);
  or or_6 (PCSel, and_6_out, comparator_8_eq, comparator_9_eq);
  Comparator #(.width(7)) comparator_30 (.a(in_1[6:0]), .b(7'b1100011), .eq(comparator_30_eq));  // open: gt, lt
  assign or_7_out = bit_extender_4_out | alu1 | bit_extender_5_out | bit_extender_6_out;  // OR_Gate or_7, 2 bits wide
  ALUSELHelper aluselhelper_1 (.in_1(in_1), .out_3(ALUSel));  // open: out_2
  Subtractor #(.width(2)) subtractor_1 (.a(or_5_out), .b(or_5_out), .out(subtractor_1_out));  // open: bin, bout
  Adder #(.width(2)) adder_1 (.a(or_7_out), .b(subtractor_1_out), .out(adder_1_out));  // open: cin, cout
  Multiplier #(.width(2)) multiplier_1 (.a(mem2), .b(2'b10), .out(multiplier_1_out));  // open: cin, cout
  Adder #(.width(2)) adder_2 (.a(adder_1_out), .b(multiplier_1_out), .out(out_13));  // open: cin, cout
  Multiplexer #(.select(2), .width(2), .enable("false")) multiplexer_1 (
    .in0(2'b00), .in1(2'b01), .in2(2'b10), .out(WBSel), .sel(out_13));  // open: in3

  // Other names for the same wires on the sheet: Opcode[6:0] = in_1[6:0]; funct3[2:0] = in_1[14:12]
endmodule

module Itype (
  input  [31:0] in_1,
  output [6:0] Opcode,
  output [4:0] rd,
  output [2:0] funct3,
  output [4:0] rs1
);


  assign funct3 = in_1[14:12];
  assign Opcode = in_1[6:0];
  assign rd = in_1[11:7];
  assign rs1 = in_1[19:15];
endmodule

module Rtype (
  input  [31:0] in_1,
  output [6:0] Opcode,
  output [4:0] rd,
  output [2:0] funct3,
  output [4:0] rs1,
  output [4:0] rs2,
  output [6:0] funct7
);


  assign funct3 = in_1[14:12];
  assign funct7 = in_1[31:25];
  assign Opcode = in_1[6:0];
  assign rd = in_1[11:7];
  assign rs1 = in_1[19:15];
  assign rs2 = in_1[24:20];
endmodule

module Stype (
  input  [31:0] in_1,
  output [6:0] Opcode,
  output [4:0] imm40,
  output [2:0] funct3,
  output [4:0] rs1,
  output [4:0] rs2
);


  assign funct3 = in_1[14:12];
  assign imm40 = in_1[11:7];
  assign Opcode = in_1[6:0];
  assign rs1 = in_1[19:15];
  assign rs2 = in_1[24:20];
endmodule

module SBtype (
  input  [31:0] in_1,
  output [6:0] Opcode,
  output [4:0] imm1141,
  output [2:0] funct3,
  output [4:0] rs1,
  output [4:0] rs2
);


  assign funct3 = in_1[14:12];
  assign imm1141 = in_1[11:7];
  assign Opcode = in_1[6:0];
  assign rs1 = in_1[19:15];
  assign rs2 = in_1[24:20];
endmodule

module Utype (
  input  [31:0] in_1,
  output [6:0] Opcode,
  output [4:0] rd
);


  assign Opcode = in_1[6:0];
  assign rd = in_1[11:7];
endmodule

module UJtype (
  input  [31:0] in_1,
  output [6:0] Opcode,
  output [4:0] rd
);


  assign Opcode = in_1[6:0];
  assign rd = in_1[11:7];
endmodule

module ImmediateGen (
  input  [31:0] Instruction,
  output [31:0] out_2
);

  wire [31:0] bit_extender_1_out, bit_extender_2_out, bit_extender_3_out, bit_extender_4_out,
       bit_extender_5_out, shifter_2_out, shifter_3_out;

  assign bit_extender_1_out = {{20{1'b0}}, {Instruction[31:25], Instruction[11:7]}};  // Bit_Extender bit_extender_1
  assign bit_extender_2_out = {{12{1'b0}}, Instruction[31:12]};  // Bit_Extender bit_extender_2
  Shifter #(.width(12)) shifter_1 (.\dist (4'b0001));  // open: in, out
  assign bit_extender_3_out = {{20{1'b0}}, Instruction[31:20]};  // Bit_Extender bit_extender_3
  assign bit_extender_4_out = {{20{1'b0}}, {Instruction[31], Instruction[7], Instruction[30:25], Instruction[11:8]}};  // Bit_Extender bit_extender_4
  Shifter #(.width(32)) shifter_2 (.in(bit_extender_4_out), .\dist (5'b00001), .out(shifter_2_out));
  assign bit_extender_5_out = {{12{1'b0}}, {Instruction[31], Instruction[19:12], Instruction[20], Instruction[30:21]}};  // Bit_Extender bit_extender_5
  Shifter #(.width(32)) shifter_3 (.in(bit_extender_5_out), .\dist (5'b00001), .out(shifter_3_out));
  Multiplexer #(.select(5), .width(32), .enable("false")) multiplexer_1 (
    .in0(bit_extender_3_out), .in4(bit_extender_3_out), .in8(bit_extender_1_out), .in13(bit_extender_2_out),
    .in24(shifter_2_out), .in25(bit_extender_3_out), .in27(shifter_3_out), .out(out_2), .sel(Instruction[6:2]));  // open: in1, in2, in3, in5, in6, in7, in9, in10, in11, in12, in14, in15, in16, in17, in18, in19, in20, in21, in22, in23, in26, in28, in29, in30, in31

  // Other names for the same wires on the sheet: opcode26[4:0] = Instruction[6:2]

  // Notes on the sheet:
  //   SB
  //   U
  //   UJ
  //   I
  //   S
endmodule

module BranchComp (
  input  [31:0] rs1,
  input  [31:0] rs2,
  input  BrUn,
  output GT,
  output EQ,
  output LT
);

  wire comparator_1_eq, comparator_1_gt, comparator_1_lt, comparator_2_lt, comparator_3_lt, comparator_4_eq,
       comparator_4_gt, comparator_4_lt, or_1_out, or_2_out;
  wire [31:0] multiplexer_1_out, multiplexer_2_out, negator_1_out, negator_2_out;

  Comparator #(.width(32)) comparator_1 (
    .a(rs1), .b(rs2), .gt(comparator_1_gt), .eq(comparator_1_eq), .lt(comparator_1_lt));
  Comparator #(.width(32)) comparator_2 (.a(rs1), .b({32{1'b0}}), .lt(comparator_2_lt));  // open: gt, eq
  Comparator #(.width(32)) comparator_3 (.a(rs2), .b({32{1'b0}}), .lt(comparator_3_lt));  // open: gt, eq
  or or_1 (or_1_out, 1'b0, comparator_2_lt);
  or or_2 (or_2_out, 1'b0, comparator_3_lt);
  Negator #(.width(32)) negator_1 (.in(rs2), .out(negator_1_out));
  Negator #(.width(32)) negator_2 (.in(rs1), .out(negator_2_out));
  Multiplexer #(.width(32), .enable("false")) multiplexer_1 (
    .in0(negator_1_out), .in1(rs2), .out(multiplexer_1_out), .sel(or_2_out));
  Multiplexer #(.width(32), .enable("false")) multiplexer_2 (
    .in0(negator_2_out), .in1(rs1), .out(multiplexer_2_out), .sel(or_1_out));
  Comparator #(.width(32)) comparator_4 (
    .a(multiplexer_2_out), .b(multiplexer_1_out), .gt(comparator_4_gt), .eq(comparator_4_eq),
    .lt(comparator_4_lt));
  Multiplexer #(.enable("false")) multiplexer_3 (.in0(comparator_1_gt), .in1(comparator_4_gt), .out(GT), .sel(BrUn));
  Multiplexer #(.enable("false")) multiplexer_4 (.in0(comparator_1_eq), .in1(comparator_4_eq), .out(EQ), .sel(BrUn));
  Multiplexer #(.enable("false")) multiplexer_5 (.in0(comparator_1_lt), .in1(comparator_4_lt), .out(LT), .sel(BrUn));
endmodule

module ALUSELHelper (
  input  [31:0] in_1,
  output out_2,
  output [3:0] out_3
);

  wire add, and1, and_1_out, and_2_out, and_3_out, and_4_out, and_5_out, and_6_out, and_7_out, and_8_out,
       and_9_out, and_10_out, and_11_out, and_12_out, and_13_out, and_14_out, and_15_out, and_17_out, bsel,
       comparator_1_eq, comparator_2_eq, comparator_3_eq, comparator_4_eq, comparator_5_eq, comparator_6_eq,
       comparator_7_eq, comparator_8_eq, comparator_9_eq, comparator_10_eq, comparator_11_eq,
       comparator_12_eq, comparator_13_eq, comparator_14_eq, comparator_15_eq, comparator_16_eq,
       comparator_17_eq, comparator_18_eq, comparator_19_eq, comparator_20_eq, comparator_21_eq,
       comparator_22_eq, comparator_23_eq, comparator_24_eq, comparator_25_eq, comparator_26_eq,
       comparator_27_eq, comparator_28_eq, comparator_29_eq, comparator_30_eq, comparator_31_eq,
       comparator_32_eq, comparator_33_eq, comparator_34_eq, comparator_35_eq, comparator_36_gt,
       comparator_36_lt, comparator_37_eq, comparator_38_eq, comparator_39_eq, comparator_40_eq,
       comparator_41_eq, comparator_42_eq, comparator_43_eq, comparator_44_eq, comparator_45_eq,
       comparator_46_eq, comparator_47_eq, comparator_48_eq, comparator_49_eq, comparator_50_eq,
       comparator_51_eq, comparator_52_eq, comparator_53_eq, comparator_54_eq, comparator_55_eq,
       comparator_56_eq, comparator_57_eq, comparator_58_eq, comparator_59_eq, comparator_60_eq,
       comparator_61_eq, comparator_62_eq, comparator_63_eq, comparator_64_eq, comparator_65_eq,
       comparator_66_eq, comparator_67_eq, comparator_68_eq, comparator_69_eq, comparator_70_eq,
       comparator_71_gt, comparator_71_lt, comparator_72_gt, comparator_72_lt, comparator_73_gt,
       comparator_73_lt, comparator_74_gt, comparator_74_lt, divu, mul, mulh, mulhu, or1, or_1_out, or_2_out,
       or_4_out, remu, sll1;
  wire [3:0] bitSetSelect, offset, starting, sumbits_1_out_2, sumbits_2_out_2, sumbits_3_out_2,
       sumbits_4_out_2;
  wire [15:3] sls;

  Comparator #(.width(7)) comparator_1 (.a(in_1[31:25]), .b({7{1'b0}}), .eq(comparator_1_eq));  // open: gt, lt
  Comparator #(.width(7)) comparator_2 (.a(in_1[6:0]), .b(7'b0110111), .eq(comparator_2_eq));  // open: gt, lt
  Comparator #(.width(7)) comparator_3 (.a(in_1[31:25]), .b({7{1'b0}}), .eq(comparator_3_eq));  // open: gt, lt
  Comparator #(.width(7)) comparator_4 (.a(in_1[31:25]), .b({7{1'b0}}), .eq(comparator_4_eq));  // open: gt, lt
  Comparator #(.width(7)) comparator_5 (.a(in_1[31:25]), .b({7{1'b0}}), .eq(comparator_5_eq));  // open: gt, lt
  Comparator #(.width(7)) comparator_6 (.a(in_1[31:25]), .b(7'b0100000), .eq(comparator_6_eq));  // open: gt, lt
  Comparator #(.width(7)) comparator_7 (.a(in_1[31:25]), .b({7{1'b0}}), .eq(comparator_7_eq));  // open: gt, lt
  Comparator #(.width(7)) comparator_8 (.a(in_1[31:25]), .b({7{1'b0}}), .eq(comparator_8_eq));  // open: gt, lt
  Comparator #(.width(7)) comparator_9 (.a(in_1[6:0]), .b(7'b0000011), .eq(comparator_9_eq));  // open: gt, lt
  Comparator #(.width(3)) comparator_10 (.a(in_1[14:12]), .b(3'b000), .eq(comparator_10_eq));  // open: gt, lt
  Comparator #(.width(3)) comparator_11 (.a(in_1[14:12]), .b(3'b000), .eq(comparator_11_eq));  // open: gt, lt
  Comparator #(.width(7)) comparator_12 (.a(in_1[6:0]), .b(7'b0110011), .eq(comparator_12_eq));  // open: gt, lt
  Comparator #(.width(3)) comparator_13 (.a(in_1[14:12]), .b(3'b110), .eq(comparator_13_eq));  // open: gt, lt
  Comparator #(.width(7)) comparator_14 (.a(in_1[6:0]), .b(7'b0110011), .eq(comparator_14_eq));  // open: gt, lt
  Comparator #(.width(3)) comparator_15 (.a(in_1[14:12]), .b(3'b100), .eq(comparator_15_eq));  // open: gt, lt
  Comparator #(.width(7)) comparator_16 (.a(in_1[6:0]), .b(7'b0110011), .eq(comparator_16_eq));  // open: gt, lt
  Comparator #(.width(3)) comparator_17 (.a(in_1[14:12]), .b(3'b010), .eq(comparator_17_eq));  // open: gt, lt
  Comparator #(.width(7)) comparator_18 (.a(in_1[31:25]), .b(7'b0000001), .eq(comparator_18_eq));  // open: gt, lt
  Comparator #(.width(7)) comparator_19 (.a(in_1[31:25]), .b(7'b0000001), .eq(comparator_19_eq));  // open: gt, lt
  Comparator #(.width(7)) comparator_20 (.a(in_1[31:25]), .b(7'b0000001), .eq(comparator_20_eq));  // open: gt, lt
  Comparator #(.width(7)) comparator_21 (.a(in_1[31:25]), .b(7'b0000001), .eq(comparator_21_eq));  // open: gt, lt
  Comparator #(.width(7)) comparator_22 (.a(in_1[31:25]), .b(7'b0100000), .eq(comparator_22_eq));  // open: gt, lt
  Comparator #(.width(7)) comparator_23 (.a(in_1[31:25]), .b(7'b0000001), .eq(comparator_23_eq));  // open: gt, lt
  Comparator #(.width(7)) comparator_24 (.a(in_1[31:25]), .b(7'b0001111), .eq(comparator_24_eq));  // open: gt, lt
  Comparator #(.width(7)) comparator_25 (.a(in_1[6:0]), .b(7'b0100011), .eq(comparator_25_eq));  // open: gt, lt
  Comparator #(.width(7)) comparator_26 (.a(in_1[6:0]), .b(7'b1100011), .eq(comparator_26_eq));  // open: gt, lt
  Comparator #(.width(7)) comparator_27 (.a(in_1[6:0]), .b(7'b1101111), .eq(comparator_27_eq));  // open: gt, lt
  Comparator #(.width(7)) comparator_28 (.a(in_1[6:0]), .b(7'b0110011), .eq(comparator_28_eq));  // open: gt, lt
  Comparator #(.width(3)) comparator_29 (.a(in_1[14:12]), .b(3'b000), .eq(comparator_29_eq));  // open: gt, lt
  Comparator #(.width(7)) comparator_30 (.a(in_1[31:25]), .b({7{1'b0}}), .eq(comparator_30_eq));  // open: gt, lt
  Comparator #(.width(3)) comparator_31 (.a(in_1[14:12]), .b(3'b000), .eq(comparator_31_eq));  // open: gt, lt
  Comparator #(.width(3)) comparator_32 (.a(in_1[14:12]), .b(3'b001), .eq(comparator_32_eq));  // open: gt, lt
  Comparator #(.width(3)) comparator_33 (.a(in_1[14:12]), .b(3'b010), .eq(comparator_33_eq));  // open: gt, lt
  Comparator #(.width(7)) comparator_34 (.a(in_1[6:0]), .b(7'b0010011), .eq(comparator_34_eq));  // open: gt, lt
  Comparator #(.width(7)) comparator_35 (.a(in_1[6:0]), .b(7'b1100111), .eq(comparator_35_eq));  // open: gt, lt
  Comparator #(.width(7)) comparator_36 (
    .a(in_1[6:0]), .b(7'b0110011), .gt(comparator_36_gt), .lt(comparator_36_lt));  // open: eq
  Comparator #(.width(7)) comparator_37 (.a(in_1[6:0]), .b(7'b0110011), .eq(comparator_37_eq));  // open: gt, lt
  Comparator #(.width(3)) comparator_38 (.a(in_1[14:12]), .b(3'b111), .eq(comparator_38_eq));  // open: gt, lt
  Comparator #(.width(7)) comparator_39 (.a(in_1[6:0]), .b(7'b0010011), .eq(comparator_39_eq));  // open: gt, lt
  Comparator #(.width(3)) comparator_40 (.a(in_1[14:12]), .b(3'b111), .eq(comparator_40_eq));  // open: gt, lt
  Comparator #(.width(7)) comparator_41 (.a(in_1[6:0]), .b(7'b0010011), .eq(comparator_41_eq));  // open: gt, lt
  Comparator #(.width(3)) comparator_42 (.a(in_1[14:12]), .b(3'b110), .eq(comparator_42_eq));  // open: gt, lt
  Comparator #(.width(7)) comparator_43 (.a(in_1[6:0]), .b(7'b0010011), .eq(comparator_43_eq));  // open: gt, lt
  Comparator #(.width(3)) comparator_44 (.a(in_1[14:12]), .b(3'b100), .eq(comparator_44_eq));  // open: gt, lt
  Comparator #(.width(7)) comparator_45 (.a(in_1[6:0]), .b(7'b0110011), .eq(comparator_45_eq));  // open: gt, lt
  Comparator #(.width(3)) comparator_46 (.a(in_1[14:12]), .b(3'b101), .eq(comparator_46_eq));  // open: gt, lt
  Comparator #(.width(7)) comparator_47 (.a(in_1[6:0]), .b(7'b0010011), .eq(comparator_47_eq));  // open: gt, lt
  Comparator #(.width(3)) comparator_48 (.a(in_1[14:12]), .b(3'b101), .eq(comparator_48_eq));  // open: gt, lt
  Comparator #(.width(7)) comparator_49 (.a(in_1[6:0]), .b(7'b0010011), .eq(comparator_49_eq));  // open: gt, lt
  Comparator #(.width(3)) comparator_50 (.a(in_1[14:12]), .b(3'b101), .eq(comparator_50_eq));  // open: gt, lt
  Comparator #(.width(7)) comparator_51 (.a(in_1[6:0]), .b(7'b0110011), .eq(comparator_51_eq));  // open: gt, lt
  Comparator #(.width(3)) comparator_52 (.a(in_1[14:12]), .b(3'b001), .eq(comparator_52_eq));  // open: gt, lt
  Comparator #(.width(7)) comparator_53 (.a(in_1[6:0]), .b(7'b0010011), .eq(comparator_53_eq));  // open: gt, lt
  Comparator #(.width(3)) comparator_54 (.a(in_1[14:12]), .b(3'b001), .eq(comparator_54_eq));  // open: gt, lt
  Comparator #(.width(7)) comparator_55 (.a(in_1[6:0]), .b(7'b0010011), .eq(comparator_55_eq));  // open: gt, lt
  Comparator #(.width(3)) comparator_56 (.a(in_1[14:12]), .b(3'b010), .eq(comparator_56_eq));  // open: gt, lt
  Comparator #(.width(7)) comparator_57 (.a(in_1[6:0]), .b(7'b0110011), .eq(comparator_57_eq));  // open: gt, lt
  Comparator #(.width(3)) comparator_58 (.a(in_1[14:12]), .b(3'b101), .eq(comparator_58_eq));  // open: gt, lt
  Comparator #(.width(7)) comparator_59 (.a(in_1[6:0]), .b(7'b0110011), .eq(comparator_59_eq));  // open: gt, lt
  Comparator #(.width(3)) comparator_60 (.a(in_1[14:12]), .b(3'b111), .eq(comparator_60_eq));  // open: gt, lt
  Comparator #(.width(7)) comparator_61 (.a(in_1[6:0]), .b(7'b0110011), .eq(comparator_61_eq));  // open: gt, lt
  Comparator #(.width(3)) comparator_62 (.a(in_1[14:12]), .b(3'b000), .eq(comparator_62_eq));  // open: gt, lt
  Comparator #(.width(7)) comparator_63 (.a(in_1[6:0]), .b(7'b0110011), .eq(comparator_63_eq));  // open: gt, lt
  Comparator #(.width(3)) comparator_64 (.a(in_1[14:12]), .b(3'b000), .eq(comparator_64_eq));  // open: gt, lt
  Comparator #(.width(7)) comparator_65 (.a(in_1[6:0]), .b(7'b0110011), .eq(comparator_65_eq));  // open: gt, lt
  Comparator #(.width(3)) comparator_66 (.a(in_1[14:12]), .b(3'b001), .eq(comparator_66_eq));  // open: gt, lt
  Comparator #(.width(7)) comparator_67 (.a(in_1[6:0]), .b(7'b0110011), .eq(comparator_67_eq));  // open: gt, lt
  Comparator #(.width(3)) comparator_68 (.a(in_1[14:12]), .b(3'b000), .eq(comparator_68_eq));  // open: gt, lt
  or or_1 (or_1_out, comparator_25_eq, comparator_26_eq, comparator_27_eq);
  or or_2 (or_2_out, comparator_31_eq, comparator_32_eq, comparator_33_eq);
  and and_1 (and_1_out, comparator_34_eq, comparator_10_eq);
  and and_2 (and_2_out, comparator_35_eq, comparator_11_eq);
  and and_3 (and_3_out, comparator_12_eq, comparator_13_eq);
  and and_4 (and_4_out, comparator_41_eq, comparator_42_eq);
  and and_5 (and_5_out, comparator_14_eq, comparator_15_eq);
  and and_6 (and_6_out, comparator_43_eq, comparator_44_eq);
  and and_7 (and_7_out, comparator_16_eq, comparator_8_eq, comparator_17_eq);
  and and_8 (and_8_out, comparator_55_eq, comparator_56_eq);
  Comparator #(.width(7)) comparator_69 (.a(in_1[6:0]), .b(7'b0110011), .eq(comparator_69_eq));  // open: gt, lt
  Comparator #(.width(3)) comparator_70 (.a(in_1[14:12]), .b(3'b011), .eq(comparator_70_eq));  // open: gt, lt
  and and_9 (and_9_out, comparator_28_eq, comparator_29_eq, comparator_30_eq);
  or or_3 (bsel, comparator_36_gt, comparator_36_lt);
  and and_10 (and_10_out, comparator_37_eq, comparator_4_eq, comparator_38_eq);
  and and_11 (and_11_out, comparator_39_eq, comparator_40_eq);
  and and_12 (and_12_out, comparator_45_eq, comparator_5_eq, comparator_46_eq);
  and and_13 (and_13_out, comparator_47_eq, comparator_1_eq, comparator_48_eq);
  and srai (sls[5], comparator_49_eq, comparator_6_eq, comparator_50_eq);
  and and_14 (and_14_out, comparator_51_eq, comparator_7_eq, comparator_52_eq);
  and and_15 (and_15_out, comparator_53_eq, comparator_3_eq, comparator_54_eq);
  and u_divu (divu, comparator_57_eq, comparator_18_eq, comparator_58_eq);
  and u_remu (remu, comparator_59_eq, comparator_19_eq, comparator_60_eq);
  and u_mul (mul, comparator_61_eq, comparator_20_eq, comparator_62_eq);
  and sub (sls[12], comparator_63_eq, comparator_22_eq, comparator_64_eq);
  and u_mulh (mulh, comparator_65_eq, comparator_23_eq, comparator_66_eq);
  and and_16 (sls[15], comparator_67_eq, comparator_24_eq, comparator_68_eq);
  or or_4 (or_4_out, or_1_out, and_9_out);
  and and_17 (and_17_out, comparator_9_eq, or_2_out);
  or u_And1 (and1, and_10_out, and_11_out);
  or u_or1 (or1, and_3_out, and_4_out);
  or xor1 (sls[3], and_5_out, and_6_out);
  or srl1 (sls[4], and_12_out, and_13_out);
  or u_sll1 (sll1, and_14_out, comparator_2_eq, and_15_out);
  or slt1 (sls[7], and_7_out, and_8_out);
  and u_mulhu (mulhu, comparator_69_eq, comparator_21_eq, comparator_70_eq);
  or u_ADD (add, or_4_out, and_17_out, and_1_out, and_2_out);
  sumBits sumbits_1 (.in_1({sls[3], or1, and1, add}), .out_2(sumbits_1_out_2));
  sumBits sumbits_2 (.in_1({sls[7], sll1, sls[5:4]}), .out_2(sumbits_2_out_2));
  sumBits sumbits_3 (.in_1({mulhu, mul, remu, divu}), .out_2(sumbits_3_out_2));
  sumBits sumbits_4 (.in_1({sls[15], mulh, bsel, sls[12]}), .out_2(sumbits_4_out_2));
  Multiplexer #(.select(4), .width(4), .enable("false")) multiplexer_1 (
    .in1(sumbits_1_out_2), .in2(sumbits_2_out_2), .in4(sumbits_3_out_2), .in8(sumbits_4_out_2), .out(offset),
    .sel({bitSetSelect[3], out_2, bitSetSelect[1:0]}));  // open: in0, in3, in5, in6, in7, in9, in10, in11, in12, in13, in14, in15
  Multiplexer #(.select(4), .width(4), .enable("false")) multiplexer_2 (
    .in0(4'b0000), .in1(4'b0001), .in2(4'b0010), .in3(4'b0011), .in4(4'b0100), .in5(4'b0101), .in6(4'b0110),
    .in7(4'b0111), .in8(4'b1000), .in9(4'b1001), .in10(4'b1010), .in11(4'b1011), .in12(4'b1100),
    .in13(4'b1101), .in14(4'b1110), .in15(4'b1111), .sel(out_3));  // open: out
  Comparator #(.width(4)) comparator_71 (
    .a(4'b0000), .b({sls[3], or1, and1, add}), .gt(comparator_71_gt), .lt(comparator_71_lt));  // open: eq
  Comparator #(.width(4)) comparator_72 (
    .a({sls[7], sll1, sls[5:4]}), .b(4'b0000), .gt(comparator_72_gt), .lt(comparator_72_lt));  // open: eq
  Comparator #(.width(4)) comparator_73 (
    .a({mulhu, mul, remu, divu}), .b(4'b0000), .gt(comparator_73_gt), .lt(comparator_73_lt));  // open: eq
  Comparator #(.width(4)) comparator_74 (
    .a({sls[15], mulh, bsel, sls[12]}), .b(4'b0000), .gt(comparator_74_gt), .lt(comparator_74_lt));  // open: eq
  or or_5 (bitSetSelect[0], comparator_71_gt, comparator_71_lt);
  or or_6 (bitSetSelect[1], comparator_72_gt, comparator_72_lt);
  or or_7 (out_2, comparator_73_gt, comparator_73_lt);
  or or_8 (bitSetSelect[3], comparator_74_gt, comparator_74_lt);
  Multiplexer #(.select(4), .width(4), .enable("false")) multiplexer_3 (
    .in1(4'b0000), .in2(4'b0100), .in4(4'b1000), .in8(4'b1100), .out(starting),
    .sel({bitSetSelect[3], out_2, bitSetSelect[1:0]}));  // open: in0, in3, in5, in6, in7, in9, in10, in11, in12, in13, in14, in15
  Adder #(.width(4)) adder_1 (.a(offset), .b(starting), .out(out_3));  // open: cin, cout

  // Other names for the same wires on the sheet: bitSetSelect[2] = out_2; Opcode[6:0] = in_1[6:0];
  //   funct3[2:0] = in_1[14:12]; funct7[6:0] = in_1[31:25]; s[3:0] = out_3;
  //   sls (some bits) = {mulh, bsel, mulhu, mul, remu, divu, sll1, or1, and1, add}; xor1 = sls[3]; srl1 = sls[4];
  //   srai = sls[5]; slt1 = sls[7]; sub = sls[12]; vaddh = sls[15]
endmodule

module sumBits (
  input  [3:0] in_1,
  output [3:0] out_2
);

  wire [2:0] adder_1_out, adder_2_out, adder_3_out, bit_extender_1_out, bit_extender_2_out,
       bit_extender_3_out, bit_extender_4_out, multiplier_1_out, multiplier_2_out, multiplier_3_out,
       multiplier_4_out;

  assign bit_extender_1_out = {{2{1'b0}}, in_1[0]};  // Bit_Extender bit_extender_1
  assign bit_extender_2_out = {{2{1'b0}}, in_1[1]};  // Bit_Extender bit_extender_2
  assign bit_extender_3_out = {{2{1'b0}}, in_1[2]};  // Bit_Extender bit_extender_3
  assign bit_extender_4_out = {{2{1'b0}}, in_1[3]};  // Bit_Extender bit_extender_4
  Multiplier #(.width(3)) multiplier_1 (.a(bit_extender_4_out), .b(3'b011), .out(multiplier_1_out));  // open: cin, cout
  Multiplier #(.width(3)) multiplier_2 (.a(3'b000), .b(bit_extender_1_out), .out(multiplier_2_out));  // open: cin, cout
  Multiplier #(.width(3)) multiplier_3 (.a(3'b001), .b(bit_extender_2_out), .out(multiplier_3_out));  // open: cin, cout
  Multiplier #(.width(3)) multiplier_4 (.a(bit_extender_3_out), .b(3'b010), .out(multiplier_4_out));  // open: cin, cout
  Adder #(.width(3)) adder_1 (.a(multiplier_4_out), .b(multiplier_1_out), .out(adder_1_out));  // open: cin, cout
  Adder #(.width(3)) adder_2 (.a(multiplier_2_out), .b(multiplier_3_out), .out(adder_2_out));  // open: cin, cout
  Adder #(.width(3)) adder_3 (.a(adder_2_out), .b(adder_1_out), .out(adder_3_out));  // open: cin, cout
  assign out_2 = {{1{1'b0}}, adder_3_out};  // Bit_Extender bit_extender_5
endmodule
