// Logisim project mem.circ as structural Verilog: 1 circuit, main circuit main
module main (
  input  [31:0] Address,
  input  Write_En,
  input  clk,
  input  [31:0] Write_Data,
  output [31:0] Read_Data
);

  wire and_1_out;

  and and_1 (and_1_out, Write_En, clk);
  RAM #(.addrWidth(14), .dataWidth(32), .bus("separate")) ram_1 (
    .addr(Address[15:2]), .din(Write_Data), .data(Read_Data), .str(Write_En), .sel(1'b1), .clk(and_1_out));  // open: ld, clr
endmodule
