// Logisim project regfile.circ as structural Verilog: 1 circuit, main circuit main
module main (
  input  [4:0] rs1,
  input  [4:0] rs2,
  input  [4:0] rd,
  input  [31:0] Write_Data,
  input  RegWEn,
  input  clk,
  output [31:0] ra,
  output [31:0] sp,
  output [31:0] t0,
  output [31:0] t1,
  output [31:0] t2,
  output [31:0] s0,
  output [31:0] s1,
  output [31:0] a0,
  output [31:0] Read_Data_1,
  output [31:0] Read_Data_2
);

  wire a0WE, and_1_out, not_1_out, raWE, s0WE, s1WE, spWE, t0WE, t1WE, t2WE;
  wire [31:0] demultiplexer_2_out0, demultiplexer_2_out1, demultiplexer_2_out2, demultiplexer_2_out5,
       demultiplexer_2_out6, demultiplexer_2_out7, demultiplexer_2_out8, demultiplexer_2_out9,
       demultiplexer_2_out10, x0;

  Demultiplexer #(.select(5), .enable("false")) demultiplexer_1 (
    .out1(raWE), .out2(spWE), .out5(t0WE), .out6(t1WE), .out7(t2WE), .out8(s0WE), .out9(s1WE), .out10(a0WE),
    .in(RegWEn), .sel(rd));  // open: out0, out3, out4, out11, out12, out13, out14, out15, out16, out17, out18, out19, out20, out21, out22, out23, out24, out25, out26, out27, out28, out29, out30, out31
  // Probe on t2WE
  // Probe on rd
  Demultiplexer #(.select(5), .width(32), .enable("false")) demultiplexer_2 (
    .out0(demultiplexer_2_out0), .out1(demultiplexer_2_out1), .out2(demultiplexer_2_out2),
    .out5(demultiplexer_2_out5), .out6(demultiplexer_2_out6), .out7(demultiplexer_2_out7),
    .out8(demultiplexer_2_out8), .out9(demultiplexer_2_out9), .out10(demultiplexer_2_out10), .in(Write_Data),
    .sel(rd));  // open: out3, out4, out11, out12, out13, out14, out15, out16, out17, out18, out19, out20, out21, out22, out23, out24, out25, out26, out27, out28, out29, out30, out31
  Multiplexer #(.select(5), .width(32), .enable("false")) multiplexer_1 (
    .in0(x0), .in1(ra), .in2(sp), .in5(t0), .in6(t1), .in7(t2), .in8(s0), .in9(s1), .in10(a0),
    .out(Read_Data_1), .sel(rs1));  // open: in3, in4, in11, in12, in13, in14, in15, in16, in17, in18, in19, in20, in21, in22, in23, in24, in25, in26, in27, in28, in29, in30, in31
  Multiplexer #(.select(5), .width(32), .enable("false")) multiplexer_2 (
    .in0(x0), .in1(ra), .in2(sp), .in5(t0), .in6(t1), .in7(t2), .in8(s0), .in9(s1), .in10(a0),
    .out(Read_Data_2), .sel(rs2));  // open: in3, in4, in11, in12, in13, in14, in15, in16, in17, in18, in19, in20, in21, in22, in23, in24, in25, in26, in27, in28, in29, in30, in31
  not not_1 (not_1_out, RegWEn);
  Register #(.width(32)) register_1 (.D(demultiplexer_2_out2), .en(spWE), .Q(sp), .clk(clk));  // open: clr
  Register #(.width(32)) register_2 (.en(t0WE), .Q(t0), .clk(clk));  // open: D, clr
  Register #(.width(32)) register_3 (.D(demultiplexer_2_out6), .en(t1WE), .Q(t1), .clk(clk));  // open: clr
  Register #(.width(32)) register_4 (.D(demultiplexer_2_out7), .en(t2WE), .Q(t2), .clk(clk));  // open: clr
  Register #(.width(32)) register_5 (.D(demultiplexer_2_out9), .en(s1WE), .Q(s1), .clk(clk));  // open: clr
  Register #(.width(32)) register_6 (.D(demultiplexer_2_out1), .en(raWE), .Q(ra), .clk(clk));  // open: clr
  Register #(.width(32)) register_7 (.D(demultiplexer_2_out8), .en(s0WE), .Q(s0), .clk(clk));  // open: clr
  Register #(.width(32)) register_8 (.D(demultiplexer_2_out10), .en(a0WE), .Q(a0), .clk(clk));  // open: clr
  and and_1 (and_1_out, not_1_out, RegWEn);
  Register #(.width(32)) register_9 (.D(demultiplexer_2_out0), .en(and_1_out), .Q(x0), .clk(clk));  // open: clr
  // Probe on demultiplexer_2_out7

  // Other names for the same wires on the sheet: read_data1[31:0] = Read_Data_1; read_data2[31:0] = Read_Data_2;
  //   read_reg1[4:0] = rs1; read_reg2[4:0] = rs2; write_en = RegWEn; write_reg[4:0] = rd

  // Notes on the sheet:
  //   INPUTS to your circuit
  //   DON'T CHANGE THE LOCATIONS OF THE INPUTS AND OUTPUTS!
  //   These are DEBUG/TEST outputs from your circuit.
  //   OUTPUTS from your circuit
endmodule
