// Logisim project run.circ as structural Verilog: 1 circuit, main circuit main
module main (
  output [31:0] ra,
  output [31:0] sp,
  output [31:0] t0,
  output [31:0] t1,
  output [31:0] t2,
  output [31:0] s0,
  output [31:0] s1,
  output [31:0] a0,
  output [31:0] Requested_Address,
  output [31:0] Requested_Instruction,
  output [15:0] Time_Step,
  output halt
);

  wire clk;

  Clock clock_1 (.out(clk));
  // Probe on Requested_Address
  cpu_main main_1 (
    .INSTRUCTION(Requested_Instruction), .CLOCK(clk), .ra(ra), .sp(sp), .t0(t0), .t1(t1), .t2(t2), .s0(s0),
    .s1(s1), .a0(a0), .FETCH_ADDRESS(Requested_Address));  // open: rd, funct3, rs1, rs2, funct7, out_13, out_12
  ROM #(.addrWidth(14), .dataWidth(32)) rom_1 (
    .addr(Requested_Address[15:2]), .data(Requested_Instruction));  // open: sel
  // Probe on Requested_Instruction
  Counter #(.width(16), .max('hffff)) counter_1 (.Q(Time_Step), .clk(clk));  // open: load, D, count, carry, clr
  Comparator #(.width(16)) comparator_1 (.a(Time_Step), .b(16'h100), .eq(halt));  // open: gt, lt

  // Other names for the same wires on the sheet: fetch_addr[31:0] = Requested_Address;
  //   Instruction[31:0] = Requested_Instruction

  // Notes on the sheet:
  //   Instruction Memory
  //   YOUR CPU SHOULD FIT IN HERE!
  //   Halts Execution After Constant # of Clock Cycles
  //   Constant
endmodule
